# Fritzing sketch main-pcb (saved by Fritzing 0.9.3b)
circuit board: 9.5cm x 7cm
breadboards: 1

parts:
  Adafruit_HUZZAH_ESP8266_Breakout1 = Adafruit HUZZAH ESP8266 Breakout [part_number=2471]
  J1 = Screw terminal - 2 pins [package=THT]
  1000μF = Electrolytic Capacitor [capacitance=1000μF package="1010 [SMD, electrolytic]"]
  V1 = DC Power [voltage=5]
  C4 = Capacitor [package=0805]
  C3 = Capacitor [package=0805]
  J2 = Camdenboss CTB0158-3 [part_number=CTB0158-3 package=THT]
  U1 = Voltage Regulator - 5V [package="TO220 [THT]"]
  Part3 = 24 NeoPixel Ring [part_number=1586]
  R5 = Resistor [tolerance=±5% resistance=470 package="0805 [SMD]"]
  Q1 = MOSFET-NCHANNEL [package=sot23-3]
  R3 = Resistor [tolerance=±5% resistance=10k package="0805 [SMD]"]
  R4 = Resistor [tolerance=±5% resistance=10k package="0805 [SMD]"]

nets:
  GND: Adafruit_HUZZAH_ESP8266_Breakout1.GND, J1.pin1, 1000μF.-, V1.V+, C4.2, C3.2, J2.pin2, U1.GND, Part3.GND
  N1: Adafruit_HUZZAH_ESP8266_Breakout1.VBat, C3.1, U1.output_voltage, Part3.VDD, R4.Pin_1
  N2: Adafruit_HUZZAH_ESP8266_Breakout1.#14, Q1.S
  N3: Adafruit_HUZZAH_ESP8266_Breakout1.3V, R3.Pin_1
  N4: J1.pin2, 1000μF.+, V1.V-, C4.1, U1.input_voltage
  N5: J2.pin3, Part3.IN, R5.Pin_1
  N6: R5.Pin_0, Q1.D, R4.Pin_0
  N7: Q1.G, R3.Pin_0

notes:
  PuckLight
  R0
  Adafruit Huzzah ESP8266
  +5V
  GND
  DATA

custom parts:
  24 NeoPixel Ring: 24 ultra bright smart LED NeoPixels are arranged in a circle with 2.6" (66mm) outer diameter. The rings are 'chainable' - connect the output pin of one to the input pin of another. Use only one microcontroller pin to control as many as you can chain together! Each LED is addressable as the driver chip is inside the LED. Each one has ~18mA constant current drive so the color will be very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
